# Fritzing sketch homesense (saved by Fritzing 0.9.2b)
breadboards: 1

parts:
  Part1 = Arduino Uno (Rev3)
  RHT1 = Humidity and Temperature Sensor RHT03
  R1 = Resistor [tolerance=±5% resistance=4.7k package=THT]
  Part2 = Bluetooth HM-10

nets:
  N1: Part1.D10_PWM/SS, Part2.RXD
  N2: Part1.D11_PWM/MOSI, Part2.TXD
  N3: Part1.D2, RHT1.Data-signal, R1.Pin_1
  VCC: Part1.3V3, RHT1.Vcc, R1.Pin_0, Part2.VCC
  GND: Part1.GND, RHT1.GND_2, Part2.GND
